// Logisim project hw4.circ as structural Verilog: 1 circuit, main circuit main
module main (
  input  x,
  output out_2
);

  wire and_1_out, and_2_out, and_3_out, and_4_out, button_1_out, clock_1_out, d_ff_1_q, d_ff_2_q, d_ff_3_q,
       or_1_out, or_2_out, s1_prime_out, s2_prime_out;

  Clock clock_1 (.out(clock_1_out));
  Button button_1 (.out(button_1_out));
  D_Flip_Flop d_ff_1 (.clk(clock_1_out), .D(s2_prime_out), .Q(d_ff_1_q), .reset(button_1_out));  // open: Qn, preset, en
  D_Flip_Flop d_ff_2 (.clk(clock_1_out), .D(s1_prime_out), .Q(d_ff_2_q), .reset(button_1_out));  // open: Qn, preset, en
  or or_1 (or_1_out, ~x, d_ff_3_q);  // OR_Gate
  or or_2 (or_2_out, d_ff_1_q, d_ff_2_q);
  and and_1 (and_1_out, x, d_ff_3_q);
  and and_2 (and_2_out, ~x, ~d_ff_3_q);  // AND_Gate
  and and_3 (and_3_out, x, d_ff_2_q, d_ff_1_q);
  and and_4 (and_4_out, ~x, ~d_ff_2_q, d_ff_1_q);  // AND_Gate
  D_Flip_Flop d_ff_3 (.clk(clock_1_out), .D(x), .Q(d_ff_3_q), .reset(button_1_out));  // open: Qn, preset, en
  and s2_prime (s2_prime_out, or_1_out, or_2_out);
  or s1_prime (s1_prime_out, and_1_out, and_2_out);
  or z (out_2, and_3_out, and_4_out);

  // Notes on the sheet:
  //   s2
  //   s1
  //   s0
  //   s2
  //   x
  //   s1
  //   changed the negates in s2, check answer 
  //   s0
  //   s0`
endmodule
